# Fritzing sketch display (saved by Fritzing 0.9.3b)

parts:
  Squix1 = OLED 0.96" 128x64 I2C SSD1306
  WeMos_D1_Mini_Protoboard_Shield1 = WeMos D1 Mini Protoboard Shield

nets:
  VCC: Squix1.VCC, WeMos_D1_Mini_Protoboard_Shield1.3V3, WeMos_D1_Mini_Protoboard_Shield1.X2-Y8
  N1: Squix1.GND, WeMos_D1_Mini_Protoboard_Shield1.G, WeMos_D1_Mini_Protoboard_Shield1.X7-Y7
  N2: Squix1.SCL, WeMos_D1_Mini_Protoboard_Shield1.D5, WeMos_D1_Mini_Protoboard_Shield1.X2-Y4
  N3: Squix1.SCA, WeMos_D1_Mini_Protoboard_Shield1.D2, WeMos_D1_Mini_Protoboard_Shield1.X7-Y4
